// Logisim project lab6.circ as structural Verilog: 18 circuits, main circuit main
module main (
  input  [63:0] in_1
);

  wire clck_out, execute_1_cnd, execute_1_overflow, execute_1_signflow, execute_1_zeroflow, fetch_1_complete,
       memory_1_complete;
  wire [3:0] fetch_1_icode, fetch_1_ifun, fetch_1_ra, fetch_1_rb;
  wire [63:0] decode_1_r8, decode_1_r9, decode_1_r10, decode_1_r11, decode_1_r12, decode_1_r13, decode_1_r14,
       decode_1_rax, decode_1_rbp, decode_1_rbx, decode_1_rcx, decode_1_rdi, decode_1_rdx, decode_1_rsi,
       decode_1_rsp, decode_1_vala, decode_1_valb, execute_1_vale, fetch_1_valc, fetch_1_valp, memory_1_valm,
       new_pc_1_newpc;

  Clock clck (.out(clck_out));
  Counter counter_1 (.clk(clck_out));  // open: load, D, count, Q, carry, up, clr
  // Probe on new_pc_1_newpc
  // Probe on fetch_1_valp
  // Probe on fetch_1_icode
  // Probe on fetch_1_ifun
  // Probe on fetch_1_ra
  // Probe on fetch_1_rb
  // Probe on fetch_1_valc
  Fetch fetch_1 (
    .PC(new_pc_1_newpc), .clk(clck_out), .reset(memory_1_complete), .icode(fetch_1_icode),
    .ifun(fetch_1_ifun), .rA(fetch_1_ra), .rB(fetch_1_rb), .valC(fetch_1_valc), .complete(fetch_1_complete),
    .valP(fetch_1_valp));  // open: imem_err, instr_val
  // Probe on execute_1_vale
  // Probe on memory_1_valm
  // Probe on decode_1_rax
  // Probe on decode_1_rcx
  // Probe on decode_1_rdx
  // Probe on decode_1_rbx
  // Probe on decode_1_rsp
  // Probe on decode_1_rbp
  // Probe on decode_1_rsi
  // Probe on decode_1_rdi
  // Probe on decode_1_r8
  // Probe on decode_1_r9
  // Probe on decode_1_r10
  // Probe on decode_1_r11
  // Probe on decode_1_r12
  // Probe on decode_1_r13
  // Probe on decode_1_r14
  Decode decode_1 (
    .icode(fetch_1_icode), .rA(fetch_1_ra), .rB(fetch_1_rb), .Write_Enable(memory_1_complete),
    .clk(clck_out), .valE(execute_1_vale), .valM(memory_1_valm), .valA(decode_1_vala), .valB(decode_1_valb),
    .rax(decode_1_rax), .rcx(decode_1_rcx), .rdx(decode_1_rdx), .rbx(decode_1_rbx), .rsp(decode_1_rsp),
    .rbp(decode_1_rbp), .rsi(decode_1_rsi), .rdi(decode_1_rdi), .r8(decode_1_r8), .r9(decode_1_r9),
    .r10(decode_1_r10), .r11(decode_1_r11), .r12(decode_1_r12), .r13(decode_1_r13), .r14(decode_1_r14));
  // Probe on decode_1_vala
  // Probe on decode_1_valb
  // Probe on execute_1_zeroflow
  // Probe on execute_1_signflow
  // Probe on execute_1_overflow
  Execute execute_1 (
    .icode(fetch_1_icode), .ifun(fetch_1_ifun), .valA(decode_1_vala), .valB(decode_1_valb),
    .valC(fetch_1_valc), .valE_enable(fetch_1_complete), .clk(clck_out), .valE(execute_1_vale),
    .cnd(execute_1_cnd), .zeroflow(execute_1_zeroflow), .signflow(execute_1_signflow),
    .overflow(execute_1_overflow));
  Memory memory_1 (
    .icode(fetch_1_icode), .valE(execute_1_vale), .valA(decode_1_vala), .valP(fetch_1_valp), .clk(clck_out),
    .enable(fetch_1_complete), .reset(memory_1_complete), .valM(memory_1_valm), .complete(memory_1_complete));
  New_PC new_pc_1 (
    .icode(fetch_1_icode), .valC(fetch_1_valc), .valM(memory_1_valm), .valP(fetch_1_valp),
    .cnd(execute_1_cnd), .enable(memory_1_complete), .clk(clck_out), .newPC(new_pc_1_newpc));
endmodule

module Fetch (
  input  [63:0] PC,
  input  clk,
  input  reset,
  output [3:0] icode,
  output [3:0] ifun,
  output [3:0] rA,
  output [3:0] rB,
  output [63:0] valC,
  output complete,
  output [63:0] valP,
  output imem_err,
  output instr_val
);

  wire comparator_1_eq, comparator_2_eq, or_1_out;
  wire [7:0] instruction_memory_1_byte9;
  wire [55:0] instruction_memory_1_byte2;

  instruction_memory instruction_memory_1 (
    .PC(PC), .clk(clk), .reset(reset), .byte0({icode, ifun}), .byte1({rA, rB}),
    .byte2(instruction_memory_1_byte2[7:0]), .byte3(instruction_memory_1_byte2[15:8]),
    .byte4(instruction_memory_1_byte2[23:16]), .byte5(instruction_memory_1_byte2[31:24]),
    .byte6(instruction_memory_1_byte2[39:32]), .byte7(instruction_memory_1_byte2[47:40]),
    .byte8(instruction_memory_1_byte2[55:48]), .byte9(instruction_memory_1_byte9), .complete(complete));
  // Probe on icode
  Comparator #(.mode("unsigned"), .width(4)) comparator_1 (
    .a(icode), .b(4'b0111), .eq(comparator_1_eq));  // open: gt, lt
  Comparator #(.mode("unsigned"), .width(4)) comparator_2 (
    .a(icode), .b(4'b1000), .eq(comparator_2_eq));  // open: gt, lt
  or or_1 (or_1_out, comparator_1_eq, comparator_2_eq);
  PC_Increment pc_increment_1 (.PC(PC), .icode(icode), .valP(valP));
  Multiplexer #(.width(64)) multiplexer_1 (
    .in0({instruction_memory_1_byte9, instruction_memory_1_byte2}),
    .in1({instruction_memory_1_byte2, rA, rB}), .out(valC), .sel(or_1_out));
endmodule

module PC_Increment (
  input  [63:0] PC,
  input  [3:0] icode,
  output [63:0] valP
);

  wire and_1_out, and_2_out, and_3_out, and_4_out, and_5_out, comparator_1_lt, comparator_2_eq,
       comparator_2_gt, comparator_2_lt, comparator_3_eq, comparator_3_gt, comparator_3_lt, comparator_4_eq,
       comparator_4_gt, comparator_4_lt, not_1_out, not_2_out, not_3_out, not_4_out, or_1_out, or_2_out;
  wire [63:0] adder_1_out, adder_2_out, adder_3_out, controlled_buffer_1_out, controlled_buffer_2_out,
       controlled_buffer_3_out, controlled_buffer_4_out;

  Comparator #(.mode("unsigned"), .width(4)) comparator_1 (
    .a(icode), .b(4'b1100), .lt(comparator_1_lt));  // open: gt, eq
  Comparator #(.mode("unsigned"), .width(4)) comparator_2 (
    .a(icode), .b(4'b0010), .gt(comparator_2_gt), .eq(comparator_2_eq), .lt(comparator_2_lt));
  Comparator #(.mode("unsigned"), .width(4)) comparator_3 (
    .a(icode), .b(4'b0110), .gt(comparator_3_gt), .eq(comparator_3_eq), .lt(comparator_3_lt));
  Comparator #(.mode("unsigned"), .width(4)) comparator_4 (
    .a(icode), .b(4'b1001), .gt(comparator_4_gt), .eq(comparator_4_eq), .lt(comparator_4_lt));
  and and_1 (and_1_out, comparator_4_lt, comparator_2_gt, comparator_3_gt);
  and and_2 (and_2_out, comparator_3_eq, comparator_2_gt);
  and and_3 (and_3_out, comparator_3_gt, comparator_4_lt);
  and and_4 (and_4_out, comparator_4_gt, comparator_1_lt);
  or or_1 (or_1_out, comparator_2_eq, and_2_out, and_4_out);
  or or_2 (or_2_out, comparator_2_lt, comparator_4_eq);
  and and_5 (and_5_out, comparator_2_gt, comparator_3_lt);
  assign controlled_buffer_1_out = or_1_out ? 64'h2 : 64'bz;  // Controlled_Buffer controlled_buffer_1
  assign controlled_buffer_2_out = or_2_out ? 64'h1 : 64'bz;  // Controlled_Buffer controlled_buffer_2
  assign controlled_buffer_3_out = and_3_out ? 64'h9 : 64'bz;  // Controlled_Buffer controlled_buffer_3
  assign controlled_buffer_4_out = and_5_out ? 64'ha : 64'bz;  // Controlled_Buffer controlled_buffer_4
  assign controlled_buffer_1_out = not_1_out ? {64{1'b0}} : 64'bz;  // Controlled_Buffer controlled_buffer_5
  not not_1 (not_1_out, or_1_out);
  not not_2 (not_2_out, and_5_out);
  assign controlled_buffer_2_out = not_3_out ? {64{1'b0}} : 64'bz;  // Controlled_Buffer controlled_buffer_6
  not not_3 (not_3_out, or_2_out);
  assign controlled_buffer_3_out = not_4_out ? {64{1'b0}} : 64'bz;  // Controlled_Buffer controlled_buffer_7
  not not_4 (not_4_out, and_3_out);
  assign controlled_buffer_4_out = not_2_out ? {64{1'b0}} : 64'bz;  // Controlled_Buffer controlled_buffer_8
  Adder #(.width(64)) adder_1 (.a(PC), .b(controlled_buffer_1_out), .out(adder_1_out));  // open: cin, cout
  Adder #(.width(64)) adder_2 (.a(adder_1_out), .b(controlled_buffer_2_out), .out(adder_2_out));  // open: cin, cout
  Adder #(.width(64)) adder_3 (.a(adder_2_out), .b(controlled_buffer_3_out), .out(adder_3_out));  // open: cin, cout
  Adder #(.width(64)) adder_4 (.a(adder_3_out), .b(controlled_buffer_4_out), .out(valP));  // open: cin, cout
endmodule

module New_PC (
  input  [3:0] icode,
  input  [63:0] valC,
  input  [63:0] valM,
  input  [63:0] valP,
  input  cnd,
  input  enable,
  input  clk,
  output [63:0] newPC
);

  wire [63:0] multiplexer_1_out, multiplexer_2_out;

  Multiplexer #(.width(64)) multiplexer_1 (.in0(valP), .in1(valC), .out(multiplexer_1_out), .sel(cnd));
  Multiplexer #(.enable("true"), .select(4), .width(64)) multiplexer_2 (
    .in0(valP), .in1(valP), .in2(valP), .in3(valP), .in4(valP), .in5(valP), .in6(valP),
    .in7(multiplexer_1_out), .in8(valC), .in9(valM), .in10(valP), .in11(valP), .out(multiplexer_2_out),
    .sel(icode), .en(enable));  // open: in12, in13, in14, in15
  Register #(.width(64)) register_1 (.D(multiplexer_2_out), .en(enable), .clk(clk), .Q(newPC));  // open: clr
endmodule

module instruction_memory (
  input  [63:0] PC,
  input  clk,
  input  reset,
  output [7:0] byte0,
  output [7:0] byte1,
  output [7:0] byte2,
  output [7:0] byte3,
  output [7:0] byte4,
  output [7:0] byte5,
  output [7:0] byte6,
  output [7:0] byte7,
  output [7:0] byte8,
  output [7:0] byte9,
  output complete
);

  wire and_1_out, comparator_1_eq, comparator_2_eq, comparator_3_eq, comparator_4_eq, comparator_5_eq,
       comparator_6_eq, comparator_7_eq, comparator_8_eq, comparator_9_eq, comparator_10_eq,
       comparator_11_eq, comparator_12_eq, controlled_buffer_1_out, controlled_buffer_3_out, not_1_out,
       not_2_out, not_3_out, not_4_out, t_ff_1_q, undriven;
  wire [7:0] rom_1_data;
  wire [63:0] adder_1_out, counter_1_q, maxcount_1_maxc;

  not not_1 (not_1_out, controlled_buffer_3_out);
  assign controlled_buffer_1_out = not_1_out ? clk : 1'bz;  // Controlled_Buffer controlled_buffer_1
  assign controlled_buffer_1_out = controlled_buffer_3_out ? not_1_out : 1'bz;  // Controlled_Buffer controlled_buffer_2
  assign controlled_buffer_3_out = reset ? not_2_out : 1'bz;  // Controlled_Buffer controlled_buffer_3
  Counter #(.max('hffffffffffffffff), .width(64)) counter_1 (
    .Q(counter_1_q), .clk(controlled_buffer_1_out), .clr(reset));  // open: load, D, count, carry, up
  assign controlled_buffer_3_out = not_2_out ? comparator_11_eq : 1'bz;  // Controlled_Buffer controlled_buffer_4
  not not_2 (not_2_out, reset);
  // Probe on counter_1_q
  // Probe on counter_1_q
  // Probe on maxcount_1_maxc
  Adder #(.width(64)) adder_1 (.a(PC), .b(counter_1_q), .out(adder_1_out));  // open: cin, cout
  ROM rom_1 (.addr(adder_1_out[7:0]), .data(rom_1_data));
  Comparator #(.width(64)) comparator_1 (.a(counter_1_q), .b({64{1'b0}}), .eq(comparator_1_eq));  // open: gt, lt
  Comparator #(.width(64)) comparator_2 (.a(counter_1_q), .b(64'h1), .eq(comparator_2_eq));  // open: gt, lt
  Comparator #(.width(64)) comparator_3 (.a(counter_1_q), .b(64'h2), .eq(comparator_3_eq));  // open: gt, lt
  Comparator #(.width(64)) comparator_4 (.a(counter_1_q), .b(64'h3), .eq(comparator_4_eq));  // open: gt, lt
  Comparator #(.width(64)) comparator_5 (.a(counter_1_q), .b(64'h4), .eq(comparator_5_eq));  // open: gt, lt
  Comparator #(.width(64)) comparator_6 (.a(counter_1_q), .b(64'h5), .eq(comparator_6_eq));  // open: gt, lt
  Comparator #(.width(64)) comparator_7 (.a(counter_1_q), .b(64'h6), .eq(comparator_7_eq));  // open: gt, lt
  Comparator #(.width(64)) comparator_8 (.a(counter_1_q), .b(64'h7), .eq(comparator_8_eq));  // open: gt, lt
  Comparator #(.width(64)) comparator_9 (.a(counter_1_q), .b(64'h8), .eq(comparator_9_eq));  // open: gt, lt
  Comparator #(.width(64)) comparator_10 (.a(counter_1_q), .b(64'h9), .eq(comparator_10_eq));  // open: gt, lt
  Comparator #(.mode("unsigned"), .width(64)) comparator_11 (
    .a(maxcount_1_maxc), .b(counter_1_q), .eq(comparator_11_eq));  // open: gt, lt
  // Probe on rom_1_data[7:4]
  T_Flip_Flop t_ff_1 (.T(comparator_11_eq), .clk(clk), .Q(t_ff_1_q), .reset(reset), .preset(t_ff_1_q));  // open: Qn
  Register #(.width(4)) register_1 (
    .D(rom_1_data[7:4]), .en(comparator_1_eq), .clk(clk), .Q(byte0[7:4]), .clr(undriven));
  Register #(.width(4)) register_2 (
    .D(rom_1_data[3:0]), .en(comparator_1_eq), .clk(clk), .Q(byte0[3:0]), .clr(undriven));
  Register #(.width(4)) register_3 (
    .D(rom_1_data[7:4]), .en(comparator_2_eq), .clk(clk), .Q(byte1[7:4]), .clr(undriven));
  Register #(.width(4)) register_4 (
    .D(rom_1_data[3:0]), .en(comparator_2_eq), .clk(clk), .Q(byte1[3:0]), .clr(undriven));
  Register register_5 (.D(rom_1_data), .en(comparator_3_eq), .clk(clk), .Q(byte2), .clr(undriven));
  Register register_6 (.D(rom_1_data), .en(comparator_4_eq), .clk(clk), .Q(byte3), .clr(undriven));
  Register register_7 (.D(rom_1_data), .en(comparator_5_eq), .clk(clk), .Q(byte4), .clr(undriven));
  Register register_8 (.D(rom_1_data), .en(comparator_6_eq), .clk(clk), .Q(byte5), .clr(undriven));
  Register register_9 (.D(rom_1_data), .en(comparator_7_eq), .clk(clk), .Q(byte6), .clr(undriven));
  Register register_10 (.D(rom_1_data), .en(comparator_8_eq), .clk(clk), .Q(byte7), .clr(undriven));
  Register register_11 (.D(rom_1_data), .en(comparator_9_eq), .clk(clk), .Q(byte8), .clr(undriven));
  Register register_12 (.D(rom_1_data), .en(comparator_10_eq), .clk(clk), .Q(byte9), .clr(undriven));
  not not_3 (not_3_out, t_ff_1_q);
  and and_1 (and_1_out, comparator_11_eq, not_3_out);
  maxCount maxcount_1 (.byte0(byte0[7:4]), .maxC(maxcount_1_maxc));
  Comparator comparator_12 (.a({8{1'b0}}), .b(byte0), .eq(comparator_12_eq));  // open: gt, lt
  assign complete = not_4_out ? and_1_out : 1'bz;  // Controlled_Buffer controlled_buffer_5
  not not_4 (not_4_out, comparator_12_eq);

  // Notes on the sheet:
  //   contents of rom_1 (hex, n*v repeats v):
  //   30 f1 16 7*0 30 f2 3 7*0 30 fa 1 7*0 20 18 30 f9 15 7*0 60 81 61 a9 76 2a 7*0 61 a2 76 1e 7*0 40 1a
  //   64 7*0 20 10 90
endmodule

module maxCount (
  input  [3:0] byte0,
  output [63:0] maxC
);

  wire and_1_out, and_2_out, and_3_out, and_4_out, comparator_1_lt, comparator_2_eq, comparator_2_gt,
       comparator_2_lt, comparator_3_eq, comparator_3_gt, comparator_3_lt, comparator_4_eq, comparator_4_gt,
       comparator_4_lt, or_1_out, or_2_out;
  wire [63:0] controlled_buffer_1_out;

  Comparator #(.mode("unsigned"), .width(4)) comparator_1 (
    .a(byte0), .b(4'b1100), .lt(comparator_1_lt));  // open: gt, eq
  Comparator #(.mode("unsigned"), .width(4)) comparator_2 (
    .a(byte0), .b(4'b0010), .gt(comparator_2_gt), .eq(comparator_2_eq), .lt(comparator_2_lt));
  Comparator #(.mode("unsigned"), .width(4)) comparator_3 (
    .a(byte0), .b(4'b0110), .gt(comparator_3_gt), .eq(comparator_3_eq), .lt(comparator_3_lt));
  Comparator #(.mode("unsigned"), .width(4)) comparator_4 (
    .a(byte0), .b(4'b1001), .gt(comparator_4_gt), .eq(comparator_4_eq), .lt(comparator_4_lt));
  and and_1 (and_1_out, comparator_3_eq, comparator_2_gt);
  and and_2 (and_2_out, comparator_3_gt, comparator_4_lt);
  and and_3 (and_3_out, comparator_2_gt, comparator_3_lt);
  and and_4 (and_4_out, comparator_4_gt, comparator_1_lt);
  or or_1 (or_1_out, comparator_2_eq, and_4_out, and_1_out);
  or or_2 (or_2_out, comparator_2_lt, comparator_4_eq);
  assign controlled_buffer_1_out = or_1_out ? 64'h2 : 64'bz;  // Controlled_Buffer controlled_buffer_1
  assign controlled_buffer_1_out = or_2_out ? 64'h1 : 64'bz;  // Controlled_Buffer controlled_buffer_2
  assign controlled_buffer_1_out = and_2_out ? 64'h9 : 64'bz;  // Controlled_Buffer controlled_buffer_3
  assign controlled_buffer_1_out = and_3_out ? 64'ha : 64'bz;  // Controlled_Buffer controlled_buffer_4
  Adder #(.width(64)) adder_1 (.a({64{1'b0}}), .b(controlled_buffer_1_out), .out(maxC));  // open: cin, cout
endmodule

module Decode (
  input  [3:0] icode,
  input  [3:0] rA,
  input  [3:0] rB,
  input  Write_Enable,
  input  clk,
  input  [63:0] valE,
  input  [63:0] valM,
  output [63:0] valA,
  output [63:0] valB,
  output [63:0] rax,
  output [63:0] rcx,
  output [63:0] rdx,
  output [63:0] rbx,
  output [63:0] rsp,
  output [63:0] rbp,
  output [63:0] rsi,
  output [63:0] rdi,
  output [63:0] r8,
  output [63:0] r9,
  output [63:0] r10,
  output [63:0] r11,
  output [63:0] r12,
  output [63:0] r13,
  output [63:0] r14
);

  wire [3:0] multiplexer_1_out, multiplexer_2_out, multiplexer_3_out, multiplexer_4_out;

  Multiplexer #(.select(4), .width(4)) multiplexer_1 (
    .in0(4'b1111), .in1(4'b1111), .in2(rA), .in3(4'b1111), .in4(rA), .in5(4'b1111), .in6(rA), .in7(rA),
    .in8(4'b1111), .in9(4'b1111), .in10(rA), .in11(4'b0100), .in12(4'b1111), .in13(4'b1111), .in14(4'b1111),
    .in15(4'b1111), .out(multiplexer_1_out), .sel(icode));
  Multiplexer #(.select(4), .width(4)) multiplexer_2 (
    .in0(4'b1111), .in1(4'b1111), .in2(4'b1111), .in3(4'b1111), .in4(rB), .in5(rB), .in6(rB), .in7(rB),
    .in8(4'b1111), .in9(4'b1111), .in10(4'b0100), .in11(4'b0100), .in12(4'b1111), .in13(4'b1111),
    .in14(4'b1111), .in15(4'b1111), .out(multiplexer_2_out), .sel(icode));
  Multiplexer #(.select(4), .width(4)) multiplexer_3 (
    .in0(4'b1111), .in1(4'b1111), .in2(rB), .in3(rB), .in4(4'b1111), .in5(4'b1111), .in6(rB), .in7(4'b1111),
    .in8(4'b1111), .in9(4'b1111), .in10(4'b0100), .in11(4'b0100), .in12(4'b1111), .in13(4'b1111),
    .in14(4'b1111), .in15(4'b1111), .out(multiplexer_3_out), .sel(icode));
  Multiplexer #(.select(4), .width(4)) multiplexer_4 (
    .in0(4'b1111), .in1(4'b1111), .in2(4'b1111), .in3(4'b1111), .in4(4'b1111), .in5(rA), .in6(4'b1111),
    .in7(4'b1111), .in8(4'b1111), .in9(4'b1111), .in10(4'b1111), .in11(rA), .in12(4'b1111), .in13(4'b1111),
    .in14(4'b1111), .in15(4'b1111), .out(multiplexer_4_out), .sel(icode));
  // Probe on multiplexer_1_out
  // Probe on multiplexer_2_out
  // Probe on multiplexer_3_out
  // Probe on multiplexer_4_out
  register_file register_file_1 (
    .icode(icode), .dstE(multiplexer_3_out), .dstM(multiplexer_4_out), .writeEnable(Write_Enable),
    .srcA(multiplexer_1_out), .srcB(multiplexer_2_out), .valE(valE), .valM(valM), .clk(clk), .valA(valA),
    .valB(valB), .rax(rax), .rcx(rcx), .rdx(rdx), .rbx(rbx), .rsp(rsp), .rbp(rbp), .rsi(rsi), .rdi(rdi),
    .r8(r8), .r9(r9), .r10(r10), .r11(r11), .r12(r12), .r13(r13), .r14(r14));
endmodule

module register_file (
  input  [3:0] icode,
  input  [3:0] dstE,
  input  [3:0] dstM,
  input  writeEnable,
  input  [3:0] srcA,
  input  [3:0] srcB,
  input  [63:0] valE,
  input  [63:0] valM,
  input  clk,
  output [63:0] valA,
  output [63:0] valB,
  output [63:0] rax,
  output [63:0] rcx,
  output [63:0] rdx,
  output [63:0] rbx,
  output [63:0] rsp,
  output [63:0] rbp,
  output [63:0] rsi,
  output [63:0] rdi,
  output [63:0] r8,
  output [63:0] r9,
  output [63:0] r10,
  output [63:0] r11,
  output [63:0] r12,
  output [63:0] r13,
  output [63:0] r14
);

  wire and_1_out, comparator_1_eq, comparator_2_eq, comparator_3_eq, comparator_4_eq, comparator_5_eq,
       comparator_6_eq, demultiplexer_2_out0, demultiplexer_2_out1, demultiplexer_2_out2,
       demultiplexer_2_out3, demultiplexer_2_out4, demultiplexer_2_out5, demultiplexer_2_out6,
       demultiplexer_2_out7, demultiplexer_2_out8, demultiplexer_2_out9, demultiplexer_2_out10,
       demultiplexer_2_out11, demultiplexer_2_out12, demultiplexer_2_out13, demultiplexer_2_out14, or_1_out,
       or_2_out;
  wire [3:0] multiplexer_1_out, multiplexer_4_out, multiplexer_5_out, register_1_q, register_2_q;
  wire [63:0] demultiplexer_1_out0, demultiplexer_1_out1, demultiplexer_1_out2, demultiplexer_1_out3,
       demultiplexer_1_out4, demultiplexer_1_out5, demultiplexer_1_out6, demultiplexer_1_out7,
       demultiplexer_1_out8, demultiplexer_1_out9, demultiplexer_1_out10, demultiplexer_1_out11,
       demultiplexer_1_out12, demultiplexer_1_out13, demultiplexer_1_out14, multiplexer_2_out,
       multiplexer_3_out;

  Comparator #(.mode("unsigned"), .width(4)) comparator_1 (
    .a(icode), .b(4'b0010), .eq(comparator_1_eq));  // open: gt, lt
  Comparator #(.mode("unsigned"), .width(4)) comparator_2 (
    .a(icode), .b(4'b0011), .eq(comparator_2_eq));  // open: gt, lt
  Comparator #(.mode("unsigned"), .width(4)) comparator_3 (
    .a(icode), .b(4'b0110), .eq(comparator_3_eq));  // open: gt, lt
  Comparator #(.mode("unsigned"), .width(4)) comparator_4 (
    .a(icode), .b(4'b1010), .eq(comparator_4_eq));  // open: gt, lt
  or or_1 (or_1_out, comparator_1_eq, comparator_2_eq, comparator_3_eq, comparator_4_eq);
  Register #(.width(4)) register_1 (.D(srcA), .en(or_1_out), .clk(clk), .Q(register_1_q));  // open: clr
  Register #(.width(4)) register_2 (.D(srcB), .en(or_1_out), .clk(clk), .Q(register_2_q));  // open: clr
  Multiplexer #(.width(4)) multiplexer_1 (.in0(dstM), .in1(dstE), .out(multiplexer_1_out), .sel(or_1_out));
  Comparator #(.mode("unsigned"), .width(4)) comparator_5 (
    .a(icode), .b(4'b1011), .eq(comparator_5_eq));  // open: gt, lt
  Multiplexer #(.width(64)) multiplexer_2 (.in0(valM), .in1(valE), .out(multiplexer_2_out), .sel(or_1_out));
  Demultiplexer #(.select(4), .width(64)) demultiplexer_1 (
    .out0(demultiplexer_1_out0), .out1(demultiplexer_1_out1), .out2(demultiplexer_1_out2),
    .out3(demultiplexer_1_out3), .out4(demultiplexer_1_out4), .out5(demultiplexer_1_out5),
    .out6(demultiplexer_1_out6), .out7(demultiplexer_1_out7), .out8(demultiplexer_1_out8),
    .out9(demultiplexer_1_out9), .out10(demultiplexer_1_out10), .out11(demultiplexer_1_out11),
    .out12(demultiplexer_1_out12), .out13(demultiplexer_1_out13), .out14(demultiplexer_1_out14),
    .in(multiplexer_2_out), .sel(multiplexer_1_out));  // open: out15
  Demultiplexer #(.select(4)) demultiplexer_2 (
    .out0(demultiplexer_2_out0), .out1(demultiplexer_2_out1), .out2(demultiplexer_2_out2),
    .out3(demultiplexer_2_out3), .out4(demultiplexer_2_out4), .out5(demultiplexer_2_out5),
    .out6(demultiplexer_2_out6), .out7(demultiplexer_2_out7), .out8(demultiplexer_2_out8),
    .out9(demultiplexer_2_out9), .out10(demultiplexer_2_out10), .out11(demultiplexer_2_out11),
    .out12(demultiplexer_2_out12), .out13(demultiplexer_2_out13), .out14(demultiplexer_2_out14),
    .in(writeEnable), .sel(multiplexer_1_out));  // open: out15
  Multiplexer #(.width(64)) multiplexer_3 (
    .in0(demultiplexer_1_out4), .in1(valE), .out(multiplexer_3_out), .sel(comparator_5_eq));
  Comparator #(.mode("unsigned"), .width(4)) comparator_6 (
    .a(icode), .b(4'b0111), .eq(comparator_6_eq));  // open: gt, lt
  or or_2 (or_2_out, comparator_5_eq, demultiplexer_2_out4);
  Multiplexer #(.width(4)) multiplexer_4 (
    .in0(srcA), .in1(register_1_q), .out(multiplexer_4_out), .sel(comparator_6_eq));
  Multiplexer #(.width(4)) multiplexer_5 (
    .in0(srcB), .in1(register_2_q), .out(multiplexer_5_out), .sel(comparator_6_eq));
  and and_1 (and_1_out, or_2_out, writeEnable);
  Register #(.width(64)) rax_0 (.D(demultiplexer_1_out0), .en(demultiplexer_2_out0), .clk(clk), .Q(rax));  // open: clr
  Register #(.width(64)) rcx_1 (.D(demultiplexer_1_out1), .en(demultiplexer_2_out1), .clk(clk), .Q(rcx));  // open: clr
  Register #(.width(64)) rdx_2 (.D(demultiplexer_1_out2), .en(demultiplexer_2_out2), .clk(clk), .Q(rdx));  // open: clr
  Register #(.width(64)) rbx_3 (.D(demultiplexer_1_out3), .en(demultiplexer_2_out3), .clk(clk), .Q(rbx));  // open: clr
  Register #(.width(64)) rsp_4 (.D(multiplexer_3_out), .en(and_1_out), .clk(clk), .Q(rsp));  // open: clr
  Register #(.width(64)) rbp_5 (.D(demultiplexer_1_out5), .en(demultiplexer_2_out5), .clk(clk), .Q(rbp));  // open: clr
  Register #(.width(64)) rsi_6 (.D(demultiplexer_1_out6), .en(demultiplexer_2_out6), .clk(clk), .Q(rsi));  // open: clr
  Register #(.width(64)) rdi_7 (.D(demultiplexer_1_out7), .en(demultiplexer_2_out7), .clk(clk), .Q(rdi));  // open: clr
  Register #(.width(64)) r8_8 (.D(demultiplexer_1_out8), .en(demultiplexer_2_out8), .clk(clk), .Q(r8));  // open: clr
  Register #(.width(64)) r9_9 (.D(demultiplexer_1_out9), .en(demultiplexer_2_out9), .clk(clk), .Q(r9));  // open: clr
  Register #(.width(64)) r10_a (
    .D(demultiplexer_1_out10), .en(demultiplexer_2_out10), .clk(clk), .Q(r10));  // open: clr
  Register #(.width(64)) r11_b (
    .D(demultiplexer_1_out11), .en(demultiplexer_2_out11), .clk(clk), .Q(r11));  // open: clr
  Register #(.width(64)) r12_c (
    .D(demultiplexer_1_out12), .en(demultiplexer_2_out12), .clk(clk), .Q(r12));  // open: clr
  Register #(.width(64)) r13_d (
    .D(demultiplexer_1_out13), .en(demultiplexer_2_out13), .clk(clk), .Q(r13));  // open: clr
  Register #(.width(64)) r14_e (
    .D(demultiplexer_1_out14), .en(demultiplexer_2_out14), .clk(clk), .Q(r14));  // open: clr
  Multiplexer #(.select(4), .width(64)) multiplexer_6 (
    .in0(rax), .in1(rcx), .in2(rdx), .in3(rbx), .in4(rsp), .in5(rbp), .in6(rsi), .in7(rdi), .in8(r8),
    .in9(r9), .in10(r10), .in11(r11), .in12(r12), .in13(r13), .in14(r14), .out(valA), .sel(multiplexer_4_out));  // open: in15
  Multiplexer #(.select(4), .width(64)) multiplexer_7 (
    .in0(rax), .in1(rcx), .in2(rdx), .in3(rbx), .in4(rsp), .in5(rbp), .in6(rsi), .in7(rdi), .in8(r8),
    .in9(r9), .in10(r10), .in11(r11), .in12(r12), .in13(r13), .in14(r14), .out(valB), .sel(multiplexer_5_out));  // open: in15
endmodule

module Execute (
  input  [3:0] icode,
  input  [3:0] ifun,
  input  [63:0] valA,
  input  [63:0] valB,
  input  [63:0] valC,
  input  valE_enable,
  input  clk,
  output [63:0] valE,
  output cnd,
  output zeroflow,
  output signflow,
  output overflow
);

  wire alu_1_overflow, alu_1_signflow, alu_1_zeroflow, and_1_out, and_2_out, and_3_out, and_4_out, and_5_out,
       and_6_out, comparator_1_eq, comparator_2_eq, comparator_3_eq, decoder_1_out0, decoder_1_out1,
       decoder_1_out2, decoder_1_out3, decoder_1_out4, decoder_1_out5, decoder_1_out6, not_1_out, not_2_out,
       or_1_out, setcc_1_scc, xnor_1_out, xnor_2_out, xor_1_out, xor_2_out;
  wire [2:0] alu_1_pcc;
  wire [3:0] controlled_buffer_1_out;
  wire [63:0] alu_1_vale, alu_a_1_a, alu_b_1_b;

  assign controlled_buffer_1_out = valE_enable ? icode : 4'bz;  // Controlled_Buffer controlled_buffer_1
  ALU_A alu_a_1 (.icode(icode), .valA(valA), .valC(valC), .A(alu_a_1_a));
  ALU_B alu_b_1 (.icode(icode), .valB(valB), .B(alu_b_1_b));
  setCC setcc_1 (.icode(controlled_buffer_1_out), .SCC(setcc_1_scc));
  ALU alu_1 (
    .A(alu_a_1_a), .B(alu_b_1_b), .ifun(ifun), .valE(alu_1_vale), .pCC(alu_1_pcc), .zeroflow(alu_1_zeroflow),
    .signflow(alu_1_signflow), .overflow(alu_1_overflow));
  Register #(.width(3)) register_1 (
    .D(alu_1_pcc), .en(setcc_1_scc), .clk(clk), .Q({overflow, signflow, zeroflow}));  // open: clr
  Register #(.width(64)) register_2 (.D(alu_1_vale), .en(valE_enable), .clk(clk), .Q(valE));  // open: clr
  Decoder #(.select(4)) decoder_1 (
    .out0(decoder_1_out0), .out1(decoder_1_out1), .out2(decoder_1_out2), .out3(decoder_1_out3),
    .out4(decoder_1_out4), .out5(decoder_1_out5), .out6(decoder_1_out6), .sel(ifun));  // open: out7, out8, out9, out10, out11, out12, out13, out14, out15, en
  not not_1 (not_1_out, comparator_1_eq);
  Comparator #(.mode("unsigned"), .width(1)) comparator_1 (
    .a(zeroflow), .b(1'b1), .eq(comparator_1_eq));  // open: gt, lt
  Comparator #(.mode("unsigned"), .width(1)) comparator_2 (
    .a(signflow), .b(1'b1), .eq(comparator_2_eq));  // open: gt, lt
  Comparator #(.mode("unsigned"), .width(1)) comparator_3 (
    .a(overflow), .b(1'b1), .eq(comparator_3_eq));  // open: gt, lt
  and and_1 (and_1_out, decoder_1_out3, comparator_1_eq);
  and and_2 (and_2_out, not_1_out, decoder_1_out4);
  not not_2 (not_2_out, comparator_1_eq);
  xnor xnor_1 (xnor_1_out, comparator_2_eq, comparator_3_eq);
  xnor xnor_2 (xnor_2_out, comparator_2_eq, comparator_3_eq);
  xor xor_1 (xor_1_out, comparator_2_eq, comparator_3_eq);
  xor xor_2 (xor_2_out, comparator_2_eq, comparator_3_eq);
  and and_3 (and_3_out, not_2_out, decoder_1_out6, xnor_1_out);
  and and_4 (and_4_out, xnor_2_out, decoder_1_out5);
  and and_5 (and_5_out, xor_1_out, decoder_1_out2);
  or or_1 (or_1_out, xor_2_out, comparator_1_eq);
  and and_6 (and_6_out, or_1_out, decoder_1_out1);
  or or_2 (cnd, decoder_1_out0, and_1_out, and_2_out, and_3_out, and_4_out, and_5_out, and_6_out);
endmodule

module ALU_A (
  input  [3:0] icode,
  input  [63:0] valA,
  input  [63:0] valC,
  output [63:0] A
);

  wire [63:0] adder_1_out, not_1_out;

  assign not_1_out = ~64'h8;  // NOT_Gate not_1, 64 bits wide
  Adder #(.width(64)) adder_1 (.a(not_1_out), .b({64{1'b0}}), .out(adder_1_out), .cin(1'b1));  // open: cout
  Multiplexer #(.select(4), .width(64)) multiplexer_1 (
    .in0({64{1'b0}}), .in1({64{1'b0}}), .in2(valA), .in3(valC), .in4(valC), .in5(valC), .in6(valA),
    .in7({64{1'b0}}), .in8(adder_1_out), .in9(64'h8), .in10(adder_1_out), .in11(64'h8), .in12({64{1'b0}}),
    .in13({64{1'b0}}), .in14({64{1'b0}}), .in15({64{1'b0}}), .out(A), .sel(icode));
endmodule

module ALU_B (
  input  [3:0] icode,
  input  [63:0] valB,
  output [63:0] B
);

  Multiplexer #(.select(4), .width(64)) multiplexer_1 (
    .in0({64{1'b0}}), .in1({64{1'b0}}), .in2({64{1'b0}}), .in3({64{1'b0}}), .in4(valB), .in5(valB),
    .in6(valB), .in7({64{1'b0}}), .in8(valB), .in9(valB), .in10(valB), .in11(valB), .in12({64{1'b0}}),
    .in13({64{1'b0}}), .in14({64{1'b0}}), .in15({64{1'b0}}), .out(B), .sel(icode));
endmodule

module ALU (
  input  [63:0] A,
  input  [63:0] B,
  input  [3:0] ifun,
  output [63:0] valE,
  output [2:0] pCC,
  output zeroflow,
  output signflow,
  output overflow
);

  wire and_2_out, and_3_out, and_4_out, and_5_out, comparator_1_lt, comparator_2_eq, comparator_3_eq,
       controlled_buffer_3_out, not_1_out, not_2_out, not_3_out, not_4_out, not_5_out, not_6_out, not_7_out,
       not_8_out, or_1_out, or_2_out, or_3_out;
  wire [1:0] controlled_buffer_1_out;
  wire [63:0] adder_1_out, and_1_out, subtractor_1_out, xor_1_out;

  Comparator #(.width(4)) comparator_1 (.a(ifun), .b(4'b0100), .lt(comparator_1_lt));  // open: gt, eq
  assign controlled_buffer_1_out = comparator_1_lt ? ifun[1:0] : 2'bz;  // Controlled_Buffer controlled_buffer_1
  not not_1 (not_1_out, comparator_1_lt);
  Adder #(.width(64)) adder_1 (.a(A), .b(B), .out(adder_1_out));  // open: cin, cout
  Subtractor #(.width(64)) subtractor_1 (.a(B), .b(A), .out(subtractor_1_out));  // open: bin, bout
  assign and_1_out = A & B;  // AND_Gate and_1, 64 bits wide
  assign xor_1_out = A ^ B;  // XOR_Gate xor_1, 64 bits wide
  assign controlled_buffer_1_out = not_1_out ? 2'b00 : 2'bz;  // Controlled_Buffer controlled_buffer_2
  Multiplexer #(.select(2), .width(64)) multiplexer_1 (
    .in0(adder_1_out), .in1(subtractor_1_out), .in2(and_1_out), .in3(xor_1_out), .out(valE),
    .sel(controlled_buffer_1_out));
  Comparator #(.width(2)) comparator_2 (.a(controlled_buffer_1_out), .b(2'b00), .eq(comparator_2_eq));  // open: gt, lt
  Comparator #(.width(2)) comparator_3 (.a(controlled_buffer_1_out), .b(2'b01), .eq(comparator_3_eq));  // open: gt, lt
  Comparator #(.width(64)) comparator_4 (.a(valE), .b({64{1'b0}}), .eq(pCC[0]), .lt(pCC[1]));  // open: gt
  and and_2 (and_2_out, valE[63], B[63], not_2_out);
  not not_2 (not_2_out, A[63]);
  not not_3 (not_3_out, valE[63]);
  not not_4 (not_4_out, B[63]);
  and and_3 (and_3_out, not_3_out, not_4_out, A[63]);
  not not_5 (not_5_out, A[63]);
  and and_4 (and_4_out, valE[63], not_5_out, not_6_out);
  not not_6 (not_6_out, B[63]);
  not not_7 (not_7_out, valE[63]);
  and and_5 (and_5_out, not_7_out, A[63], B[63]);
  assign controlled_buffer_3_out = comparator_2_eq ? or_2_out : 1'bz;  // Controlled_Buffer controlled_buffer_3
  or or_1 (or_1_out, and_2_out, and_3_out);
  or or_2 (or_2_out, and_4_out, and_5_out);
  or or_3 (or_3_out, comparator_2_eq, comparator_3_eq);
  assign controlled_buffer_3_out = comparator_3_eq ? or_1_out : 1'bz;  // Controlled_Buffer controlled_buffer_4
  Multiplexer multiplexer_2 (.in0(1'b0), .in1(controlled_buffer_3_out), .out(overflow), .sel(or_3_out));
  not not_8 (not_8_out, pCC[1]);
  // AND_Gate and_6 has open pins: in0=overflow, in1=not_8_out, out=open

  assign pCC[2] = overflow;
  assign signflow = pCC[1];
  assign zeroflow = pCC[0];
endmodule

module setCC (
  input  [3:0] icode,
  output SCC
);

  wire comparator_1_eq, comparator_2_eq, comparator_3_eq;

  Comparator #(.width(4)) comparator_1 (.a(icode), .b(4'b0010), .eq(comparator_1_eq));  // open: gt, lt
  Comparator #(.width(4)) comparator_2 (.a(icode), .b(4'b0110), .eq(comparator_2_eq));  // open: gt, lt
  Comparator #(.width(4)) comparator_3 (.a(icode), .b(4'b0111), .eq(comparator_3_eq));  // open: gt, lt
  or or_1 (SCC, comparator_1_eq, comparator_2_eq);
endmodule

module Memory (
  input  [3:0] icode,
  input  [63:0] valE,
  input  [63:0] valA,
  input  [63:0] valP,
  input  clk,
  input  enable,
  input  reset,
  output [63:0] valM,
  output complete
);

  wire and_1_out, and_2_out, comparator_1_eq, comparator_2_eq, comparator_3_eq, comparator_4_eq,
       comparator_5_eq, comparator_6_eq, comparator_7_eq, controlled_buffer_1_out, mem_r_1_read,
       mem_w_1_write, or_1_out, register_1_q, register_3_q, register_4_q, register_5_q, register_6_q,
       register_7_q, register_8_q, register_9_q, t_ff_1_q, undriven;
  wire [2:0] controlled_buffer_2_out, counter_1_q, register_2_q;
  wire [7:0] adder_1_out, controlled_buffer_3_out, mem_addr_1_address, mem_addr_1_address_2,
       mem_addr_1_address_3, mem_addr_1_address_4, mem_addr_1_address_5, mem_addr_1_address_6,
       mem_addr_1_address_7, mem_addr_1_address_8, mem_data_1_data, mem_data_1_data_2, mem_data_1_data_3,
       mem_data_1_data_4, mem_data_1_data_5, mem_data_1_data_6, mem_data_1_data_7, mem_data_1_data_8,
       multiplexer_1_out, ram_1_dout, register_11_q, register_12_q, register_13_q, register_14_q,
       register_15_q, register_16_q, register_17_q;

  Register #(.width(1)) register_1 (.D(enable), .clk(clk), .Q(register_1_q));  // open: en, clr
  and and_1 (and_1_out, register_1_q, or_1_out);
  T_Flip_Flop t_ff_1 (.T(register_1_q), .Q(t_ff_1_q), .reset(reset), .preset(and_1_out));  // open: clk, Qn
  or or_1 (or_1_out, mem_w_1_write, mem_r_1_read);
  Counter #(.max('h7), .width(3)) counter_1 (
    .Q(counter_1_q), .clk(controlled_buffer_1_out), .clr(reset));  // open: load, D, count, carry, up
  assign controlled_buffer_1_out = t_ff_1_q ? clk : 1'bz;  // Controlled_Buffer controlled_buffer_1
  mem_r mem_r_1 (.icode(icode), .read(mem_r_1_read));
  mem_w mem_w_1 (.icode(icode), .write(mem_w_1_write));
  mem_addr mem_addr_1 (
    .icode(icode), .valA(valA), .valE(valE),
    .address({mem_addr_1_address_8, mem_addr_1_address_7, mem_addr_1_address_6, mem_addr_1_address_5, mem_addr_1_address_4, mem_addr_1_address_3, mem_addr_1_address_2, mem_addr_1_address}));
  mem_data mem_data_1 (
    .icode(icode), .valA(valA), .valP(valP),
    .data({mem_data_1_data_8, mem_data_1_data_7, mem_data_1_data_6, mem_data_1_data_5, mem_data_1_data_4, mem_data_1_data_3, mem_data_1_data_2, mem_data_1_data}));
  Register #(.width(3)) register_2 (.D(counter_1_q), .clk(clk), .Q(register_2_q));  // open: en, clr
  Register #(.width(1)) register_3 (.D(register_1_q), .clk(clk), .Q(register_3_q), .clr(reset));  // open: en
  and and_2 (and_2_out, mem_w_1_write, t_ff_1_q);
  assign controlled_buffer_2_out = t_ff_1_q ? register_2_q : 3'bz;  // Controlled_Buffer controlled_buffer_2
  Register #(.width(1)) register_4 (.D(register_3_q), .clk(clk), .Q(register_4_q), .clr(reset));  // open: en
  Register #(.width(1)) register_5 (.D(register_4_q), .clk(clk), .Q(register_5_q), .clr(reset));  // open: en
  Register #(.width(1)) register_6 (.D(register_5_q), .clk(clk), .Q(register_6_q), .clr(reset));  // open: en
  Comparator #(.mode("unsigned"), .width(3)) comparator_1 (
    .a(controlled_buffer_2_out), .b(3'b000), .eq(comparator_1_eq));  // open: gt, lt
  Comparator #(.mode("unsigned"), .width(3)) comparator_2 (
    .a(controlled_buffer_2_out), .b(3'b001), .eq(comparator_2_eq));  // open: gt, lt
  Comparator #(.mode("unsigned"), .width(3)) comparator_3 (
    .a(controlled_buffer_2_out), .b(3'b010), .eq(comparator_3_eq));  // open: gt, lt
  Comparator #(.mode("unsigned"), .width(3)) comparator_4 (
    .a(controlled_buffer_2_out), .b(3'b011), .eq(comparator_4_eq));  // open: gt, lt
  Comparator #(.mode("unsigned"), .width(3)) comparator_5 (
    .a(controlled_buffer_2_out), .b(3'b100), .eq(comparator_5_eq));  // open: gt, lt
  Comparator #(.mode("unsigned"), .width(3)) comparator_6 (
    .a(controlled_buffer_2_out), .b(3'b101), .eq(comparator_6_eq));  // open: gt, lt
  Comparator #(.mode("unsigned"), .width(3)) comparator_7 (
    .a(controlled_buffer_2_out), .b(3'b110), .eq(comparator_7_eq));  // open: gt, lt
  Comparator #(.mode("unsigned"), .width(3)) comparator_8 (
    .a(controlled_buffer_2_out), .b(3'b111));  // open: gt, eq, lt
  Register #(.width(1)) register_7 (.D(register_6_q), .clk(clk), .Q(register_7_q), .clr(reset));  // open: en
  Register #(.width(1)) register_8 (.D(register_7_q), .clk(clk), .Q(register_8_q), .clr(reset));  // open: en
  Adder adder_1 (.a(mem_addr_1_address), .b({{5{1'b0}}, counter_1_q}), .out(adder_1_out));  // open: cin, cout
  Multiplexer #(.select(3), .width(8)) multiplexer_1 (
    .in0(mem_data_1_data), .in1(mem_data_1_data_2), .in2(mem_data_1_data_3), .in3(mem_data_1_data_4),
    .in4(mem_data_1_data_5), .in5(mem_data_1_data_6), .in6(mem_data_1_data_7), .in7(mem_data_1_data_8),
    .out(multiplexer_1_out), .sel(counter_1_q));
  Register #(.width(1)) register_9 (.D(register_8_q), .clk(clk), .Q(register_9_q), .clr(reset));  // open: en
  Register #(.width(1)) register_10 (.D(register_9_q), .clk(clk), .Q(complete), .clr(undriven));  // open: en
  RAM ram_1 (
    .addr(adder_1_out), .we(and_2_out), .oe(mem_r_1_read), .clk(clk), .din(multiplexer_1_out),
    .dout(ram_1_dout));
  assign controlled_buffer_3_out = mem_r_1_read ? ram_1_dout : 8'bz;  // Controlled_Buffer controlled_buffer_3
  Register register_11 (.D(controlled_buffer_3_out), .en(comparator_1_eq), .clk(clk), .Q(register_11_q));  // open: clr
  Register register_12 (.D(controlled_buffer_3_out), .en(comparator_2_eq), .clk(clk), .Q(register_12_q));  // open: clr
  Register register_13 (.D(controlled_buffer_3_out), .en(comparator_3_eq), .clk(clk), .Q(register_13_q));  // open: clr
  Register register_14 (.D(controlled_buffer_3_out), .en(comparator_4_eq), .clk(clk), .Q(register_14_q));  // open: clr
  Register register_15 (.D(controlled_buffer_3_out), .en(comparator_5_eq), .clk(clk), .Q(register_15_q));  // open: clr
  Register register_16 (.D(controlled_buffer_3_out), .en(comparator_6_eq), .clk(clk), .Q(register_16_q));  // open: clr
  Register register_17 (.D(controlled_buffer_3_out), .en(comparator_7_eq), .clk(clk), .Q(register_17_q));  // open: clr
  assign valM = mem_r_1_read ? {controlled_buffer_3_out, register_17_q, register_16_q, register_15_q, register_14_q, register_13_q, register_12_q, register_11_q} : 64'bz;  // Controlled_Buffer controlled_buffer_4
endmodule

module mem_addr (
  input  [3:0] icode,
  input  [63:0] valA,
  input  [63:0] valE,
  output [63:0] address
);

  Multiplexer #(.select(4), .width(64)) multiplexer_1 (
    .in0({64{1'b0}}), .in1({64{1'b0}}), .in2({64{1'b0}}), .in3({64{1'b0}}), .in4(valE), .in5(valE),
    .in6({64{1'b0}}), .in7({64{1'b0}}), .in8(valE), .in9(valA), .in10(valE), .in11(valA), .in12({64{1'b0}}),
    .in13({64{1'b0}}), .in14({64{1'b0}}), .in15({64{1'b0}}), .out(address), .sel(icode));
endmodule

module mem_data (
  input  [3:0] icode,
  input  [63:0] valA,
  input  [63:0] valP,
  output [63:0] data
);

  Multiplexer #(.select(4), .width(64)) multiplexer_1 (
    .in0({64{1'b0}}), .in1({64{1'b0}}), .in2({64{1'b0}}), .in3({64{1'b0}}), .in4(valA), .in5({64{1'b0}}),
    .in6({64{1'b0}}), .in7({64{1'b0}}), .in8(valP), .in9({64{1'b0}}), .in10(valA), .in11({64{1'b0}}),
    .in12({64{1'b0}}), .in13({64{1'b0}}), .in14({64{1'b0}}), .in15({64{1'b0}}), .out(data), .sel(icode));
endmodule

module mem_w (
  input  [3:0] icode,
  output write
);

  wire comparator_1_eq, comparator_2_eq, comparator_3_eq;

  Comparator #(.mode("unsigned"), .width(4)) comparator_1 (
    .a(icode), .b(4'b0100), .eq(comparator_1_eq));  // open: gt, lt
  Comparator #(.mode("unsigned"), .width(4)) comparator_2 (
    .a(icode), .b(4'b1000), .eq(comparator_2_eq));  // open: gt, lt
  Comparator #(.mode("unsigned"), .width(4)) comparator_3 (
    .a(icode), .b(4'b1010), .eq(comparator_3_eq));  // open: gt, lt
  or or_1 (write, comparator_1_eq, comparator_2_eq, comparator_3_eq);
endmodule

module mem_r (
  input  [3:0] icode,
  output read
);

  wire comparator_1_eq, comparator_2_eq, comparator_3_eq;

  Comparator #(.mode("unsigned"), .width(4)) comparator_1 (
    .a(icode), .b(4'b0101), .eq(comparator_1_eq));  // open: gt, lt
  Comparator #(.mode("unsigned"), .width(4)) comparator_2 (
    .a(icode), .b(4'b1001), .eq(comparator_2_eq));  // open: gt, lt
  Comparator #(.mode("unsigned"), .width(4)) comparator_3 (
    .a(icode), .b(4'b1011), .eq(comparator_3_eq));  // open: gt, lt
  or or_1 (read, comparator_1_eq, comparator_2_eq, comparator_3_eq);
endmodule
